// Logisim project cpu.circ as structural Verilog: 3 circuits, main circuit main
module main (
  input  [3:0] ALU_op,
  input  [1:0] A_src,
  input  [1:0] B_src,
  input  C_write,
  input  data_src,
  input  X_write,
  input  [1:0] addr_src,
  input  [1:0] ACCUM_src,
  input  ACCUM_write,
  input  oper_write,
  input  IR_write,
  input  PC_write,
  input  mem_write
);

  wire alu_1_c_out, alu_1_n, alu_1_v, alu_1_z, CLOCK_out, d_ff_1_q, not_1_out;
  wire [7:0] STATE_q;
  wire [15:0] ACCUM_q, alu_1_result, IR_q, multiplexer_1_out, multiplexer_2_out, multiplexer_3_out,
       multiplexer_4_out, multiplexer_5_out, OPER_q, PC_q, ram_1_data, rom_1_data, X_q;

  Clock CLOCK (.out(CLOCK_out));
  Register #(.width(16)) PC (.D(alu_1_result), .en(PC_write), .Q(PC_q), .clk(CLOCK_out));  // open: clr
  Register STATE (.Q(STATE_q), .clk(CLOCK_out));  // open: D, en, clr
  Multiplexer #(.select(2), .width(16)) multiplexer_1 (
    .in0(ACCUM_q), .in1(PC_q), .out(multiplexer_1_out), .sel(A_src));  // open: in2, in3
  Multiplexer #(.width(16)) multiplexer_2 (.in0(ACCUM_q), .in1(alu_1_result), .out(multiplexer_2_out), .sel(data_src));
  Multiplexer #(.select(2), .width(16)) multiplexer_3 (
    .in0(PC_q), .in1(OPER_q), .out(multiplexer_3_out), .sel(addr_src));  // open: in2, in3
  RAM #(.addrWidth(16), .dataWidth(16), .bus("separate")) ram_1 (
    .addr(multiplexer_3_out), .din(multiplexer_2_out), .data(ram_1_data), .str(mem_write), .clk(CLOCK_out),
    .ld(not_1_out));  // open: sel, clr
  not not_1 (not_1_out, mem_write);
  ROM #(.dataWidth(16)) rom_1 (.addr(STATE_q), .data(rom_1_data));  // open: sel
  Multiplexer #(.select(2), .width(16)) multiplexer_4 (
    .in0({16{1'b0}}), .in1(16'h1), .in2(OPER_q), .out(multiplexer_4_out), .sel(B_src));  // open: in3
  Register #(.width(16)) OPER (.D(ram_1_data), .en(oper_write), .Q(OPER_q), .clk(CLOCK_out));  // open: clr
  alu alu_1 (
    .oper(ALU_op), .A(multiplexer_1_out), .B(multiplexer_4_out), .C_in(d_ff_1_q), .Z(alu_1_z),
    .Result(alu_1_result), .C_out(alu_1_c_out), .N(alu_1_n), .V(alu_1_v));
  Register #(.width(16)) IR (.D(ram_1_data), .en(IR_write), .Q(IR_q), .clk(CLOCK_out));  // open: clr
  Multiplexer #(.select(2), .width(16)) multiplexer_5 (
    .in0(ram_1_data), .in1(alu_1_result), .out(multiplexer_5_out), .sel(ACCUM_src));  // open: in2, in3
  Register #(.width(16)) ACCUM (.D(multiplexer_5_out), .en(ACCUM_write), .Q(ACCUM_q), .clk(CLOCK_out));  // open: clr
  D_Flip_Flop d_ff_1 (.clk(CLOCK_out), .D(alu_1_c_out), .Q(d_ff_1_q), .en(C_write));  // open: Qn, preset, reset
  Register #(.width(16)) X (.D(ram_1_data), .en(X_write), .Q(X_q), .clk(CLOCK_out));  // open: clr

  // Notes on the sheet:
  //   contents of rom_1 (hex, n*v repeats v):
  //   c000
endmodule

module alu (
  input  [3:0] oper,
  input  [15:0] A,
  input  [15:0] B,
  input  C_in,
  output Z,
  output [15:0] Result,
  output C_out,
  output N,
  output V
);

  wire adder_1_cout, subtractor_1_bout;
  wire [15:0] adder_1_out, subtractor_1_out;

  Adder #(.width(16)) adder_1 (.a(B), .b(A), .out(adder_1_out), .cin(C_in), .cout(adder_1_cout));
  Subtractor #(.width(16)) subtractor_1 (.a(A), .b(B), .out(subtractor_1_out), .bin(C_in), .bout(subtractor_1_bout));
  Multiplexer #(.select(4), .width(16)) multiplexer_1 (
    .in0(adder_1_out), .in1(subtractor_1_out), .out({N, Result[14:0]}), .sel(oper));  // open: in2, in3, in4, in5, in6, in7, in8, in9, in10, in11, in12, in13, in14, in15
  Multiplexer #(.select(4)) multiplexer_2 (
    .in0(adder_1_cout), .in1(subtractor_1_bout), .out(C_out), .sel(oper));  // open: in2, in3, in4, in5, in6, in7, in8, in9, in10, in11, in12, in13, in14, in15
  Pull_Resistor pull_resistor_1 (.node({N, Result[14:0]}));
  nor nor_1 (Z, Result[0], Result[1], Result[2], Result[3], Result[4], Result[5], Result[6], Result[7], Result[8], Result[9], Result[10], Result[11], Result[12], Result[13], Result[14], N);
  Pull_Resistor pull_resistor_2 (.node(C_out));
  overflow overflow_1 (.a(A[15]), .b(B[15]), .r(N), .v(V));
  Pull_Resistor pull_resistor_3 (.node(V));

  assign Result[15] = N;

  // Notes on the sheet:
  //   add adc, sbc and disable carry for add and sub
endmodule

module overflow (
  input  a,
  input  b,
  input  r,
  output v
);

  wire and_1_out, and_2_out, and_3_out, and_4_out, not_1_out, not_2_out, not_3_out;

  not not_1 (not_1_out, a);
  not not_2 (not_2_out, b);
  and and_1 (and_1_out, not_1_out, not_2_out);
  and and_2 (and_2_out, a, b);
  not not_3 (not_3_out, r);
  and and_3 (and_3_out, and_1_out, r);
  and and_4 (and_4_out, and_2_out, not_3_out);
  or or_1 (v, and_3_out, and_4_out);
endmodule
